// Digital circuit 74175.dig as structural Verilog
module _74175 (
  input  _1D,
  input  _2D,
  input  _3D,
  input  _4D,
  input  VCC,
  input  GND,
  input  CLK,
  input  nCLR,
  output _1Q,
  output n1Q,
  output _2Q,
  output n2Q,
  output _3Q,
  output n3Q,
  output _4Q,
  output n4Q
);

  wire not_1_out, pulldown_1_out;

  not not_1 (not_1_out, nCLR);
  PowerSupply powersupply_1 (.VDD(VCC), .GND(GND));
  PullDown pulldown_1 (.out(pulldown_1_out));
  D_FF_AS d_ff_as_1 (.Set(pulldown_1_out), .D(_1D), .C(CLK), .Clr(not_1_out), .Q(_1Q), .nQ(n1Q));
  D_FF_AS d_ff_as_2 (.Set(pulldown_1_out), .D(_2D), .C(CLK), .Clr(not_1_out), .Q(_2Q), .nQ(n2Q));
  D_FF_AS d_ff_as_3 (.Set(pulldown_1_out), .D(_3D), .C(CLK), .Clr(not_1_out), .Q(_3Q), .nQ(n3Q));
  D_FF_AS d_ff_as_4 (.Set(pulldown_1_out), .D(_4D), .C(CLK), .Clr(not_1_out), .Q(_4Q), .nQ(n4Q));

  // Notes on the sheet:
  //   _1Q: pin 2
  //   n1Q: pin 3
  //   _1D: pin 4
  //   _2Q: pin 7
  //   n2Q: pin 6
  //   _2D: pin 5
  //   _3Q: pin 10
  //   n3Q: pin 11
  //   _3D: pin 12
  //   _4Q: pin 15
  //   n4Q: pin 14
  //   _4D: pin 13
  //   VCC: pin 16, default 1
  //   GND: pin 8
  //   CLK: pin 9
  //   nCLR: pin 1
endmodule
