// Digital circuit 7475.dig as structural Verilog
module _7475 (
  input  D0,
  input  G1_2,
  input  D1,
  input  D2,
  input  G3_4,
  input  D3,
  input  VCC,
  input  GND,
  output Q0,
  output Q1,
  output Q2,
  output Q3,
  output nQ0,
  output nQ1,
  output nQ2,
  output nQ3
);

  wire and_1_out, and_2_out, and_3_out, and_4_out, and_5_out, and_6_out, and_7_out, and_8_out;

  PowerSupply powersupply_1 (.VDD(VCC), .GND(GND));
  and and_1 (and_1_out, G1_2, D0);
  and and_2 (and_2_out, G1_2, ~D0);  // And
  and and_3 (and_3_out, G1_2, D1);
  and and_4 (and_4_out, G1_2, ~D1);  // And
  and and_5 (and_5_out, G3_4, D2);
  and and_6 (and_6_out, G3_4, ~D2);  // And
  and and_7 (and_7_out, G3_4, D3);
  and and_8 (and_8_out, G3_4, ~D3);  // And
  RS_FF_AS rs_ff_as_1 (.S(and_1_out), .R(and_2_out), .Q(Q0), .nQ(nQ0));
  RS_FF_AS rs_ff_as_2 (.S(and_3_out), .R(and_4_out), .Q(Q1), .nQ(nQ1));
  RS_FF_AS rs_ff_as_3 (.S(and_5_out), .R(and_6_out), .Q(Q2), .nQ(nQ2));
  RS_FF_AS rs_ff_as_4 (.S(and_7_out), .R(and_8_out), .Q(Q3), .nQ(nQ3));

  // Notes on the sheet:
  //   D0: pin 2
  //   Q0: pin 16
  //   G1_2: pin 13
  //   D1: pin 3
  //   Q1: pin 15
  //   D2: pin 6
  //   Q2: pin 10
  //   G3_4: pin 4
  //   D3: pin 7
  //   Q3: pin 9
  //   nQ0: pin 1
  //   nQ1: pin 14
  //   nQ2: pin 11
  //   nQ3: pin 8
  //   VCC: pin 5, default 1
  //   GND: pin 12
endmodule
