// Digital circuit 7495.dig as structural Verilog
module _7495 (
  input  P0,
  input  S,
  input  DS,
  input  nCP1,
  input  nCP2,
  input  P1,
  input  P2,
  input  P3,
  input  VCC,
  input  GND,
  output Q0,
  output Q1,
  output Q2,
  output Q3
);

  wire and_1_out, and_2_out, and_3_out, and_4_out, and_5_out, and_6_out, and_7_out, and_8_out, and_9_out,
       and_10_out, nor_1_out, nor_2_out, nor_3_out, nor_4_out, not_1_out, not_2_out, not_3_out, not_4_out,
       not_5_out, not_6_out, or_1_out;

  PowerSupply powersupply_1 (.VDD(VCC), .GND(GND));
  not not_1 (not_1_out, S);
  and and_1 (and_1_out, not_1_out, nCP1);
  and and_2 (and_2_out, S, nCP2);
  not not_2 (not_2_out, not_1_out);
  or or_1 (or_1_out, and_1_out, and_2_out);
  and and_3 (and_3_out, not_1_out, DS);
  nor nor_1 (nor_1_out, and_4_out, and_3_out);
  not not_3 (not_3_out, nor_1_out);
  and and_4 (and_4_out, P0, not_2_out);
  RS_FF rs_ff_1 (.S(not_3_out), .C(or_1_out), .R(nor_1_out), .Q(Q0));  // open: nQ
  and and_5 (and_5_out, not_1_out, Q0);
  nor nor_2 (nor_2_out, and_6_out, and_5_out);
  not not_4 (not_4_out, nor_2_out);
  and and_6 (and_6_out, P1, not_2_out);
  RS_FF rs_ff_2 (.S(not_4_out), .C(or_1_out), .R(nor_2_out), .Q(Q1));  // open: nQ
  and and_7 (and_7_out, not_1_out, Q1);
  nor nor_3 (nor_3_out, and_8_out, and_7_out);
  not not_5 (not_5_out, nor_3_out);
  and and_8 (and_8_out, P2, not_2_out);
  RS_FF rs_ff_3 (.S(not_5_out), .C(or_1_out), .R(nor_3_out), .Q(Q2));  // open: nQ
  and and_9 (and_9_out, not_1_out, Q2);
  nor nor_4 (nor_4_out, and_10_out, and_9_out);
  not not_6 (not_6_out, nor_4_out);
  and and_10 (and_10_out, P3, not_2_out);
  RS_FF rs_ff_4 (.S(not_6_out), .C(or_1_out), .R(nor_4_out), .Q(Q3));  // open: nQ

  // Notes on the sheet:
  //   Q0: pin 13
  //   P0: pin 2
  //   S: pin 6
  //   DS: pin 1
  //   nCP1: pin 9
  //   nCP2: pin 8
  //   Q1: pin 12
  //   P1: pin 3
  //   Q2: pin 11
  //   P2: pin 4
  //   Q3: pin 10
  //   P3: pin 5
  //   VCC: pin 14, default 1
  //   GND: pin 7
endmodule
