// Digital circuit JAWS_Top_Level_1.dig as structural Verilog
module JAWS_Top_Level_1 (
  input  clk,
  input  RUN,
  input  in_3,
  input  in_4,
  input  in_5,
  input  in_6,
  input  in_7
);

  wire _7401_5_pin3, _7401_5_pin6, _7401_5_pin9, _7401_5_pin12, _7401_6_pin1, _7401_6_pin4, _7401_6_pin13,
       _7401_7_pin3, _7401_7_pin6, _7401_7_pin9, _7401_7_pin12, _7474_1_pin3, _7474_1_pin5, _7474_1_pin6,
       _7474_1_pin8, _7474_1_pin9, _7475_1_nq1, _7475_1_nq2, _7475_1_q1, _7475_1_q2, _62256_1_p22,
       _74151_1_pin12, _74151_1_pin13, _74151_1_pin14, _74151_1_pin15, _74163_1_pin12, _74163_1_pin13,
       _74163_1_pin14, _74175_1__1q, _74175_1__2q, _74175_1__3q, _74175_1__4q, _74181_1_pin7, _74193_1_pin4,
       _74193_1_pin5, _74193_2_pin4, _74193_2_pin5, _74193_3_pin4, _74193_3_pin5, A0, A0__gt_BUS, A1,
       A1__gt_BUS, A2, A3, A4, A5, A6, A7, A8, A9, A10, A11, A12, A13, A14, A15, and_1_out, and_2_out,
       and_3_out, and_4_out, and_5_out, and_6_out, and_7_out, and_8_out, and_9_out, BUS0, BUS1, BUS2, BUS3,
       BUS4, BUS5, BUS6, BUS7, BUS__gt_N, BUS__gt_P, BUS__gt_R, BUS__gt_X, C0, C1, C2, C3, C4, C5, C6, C7,
       C8, C9, C10, C11, C12, C13, C14, C15, CLR_2, Cn, Cn_plus_8, D__gt_BUS, D_Bit_0, D_Bit_1, D_Bit_2,
       D_Bit_3, D_Bit_4, D_Bit_5, D_Bit_6, D_Bit_7, D_CLOCK, DE_REG, DF, EF1, EF2, EF3, EF4, F0, F1, F2, F3,
       F4, F5, F6, F7, I0, I1, I2, I3_COND_eq_1, I4, I6, I7, I8, I9, IF, INH_N, INH_N_DECODE, INH_R00,
       INH_R01, INH_R10, INT_REG, LOAD, M, M__gt_BUS, monoflop_1_q, N0, N1, N2, N3, N_1_9, N_2_A, N_6_E,
       N__gt_BUS, nand_2_out, nand_3_out, nand_4_out, nand_5_out, nand_6_out, nand_7_out, nand_9_out,
       nand_13_out, nand_14_out, nand_16_out, nand_17_out, nand_18_out, nand_19_out, nand_20_out,
       nand_21_out, nand_22_out, nand_23_out, nand_24_out, nand_25_out, nand_33_out, nand_35_out,
       nand_37_out, nand_38_out, nand_44_out, nand_45_out, nand_46_out, nand_54_out, nand_55_out,
       nand_56_out, nand_58_out, nand_61_out, nand_62_out, nand_64_out, nand_67_out, nand_68_out,
       nand_69_out, nand_70_out, nand_71_out, nand_75_out, nand_76_out, nand_77_out, nand_79_out,
       nand_82_out, nand_83_out, NBIT0, NBIT1, NBIT2, NBIT3, nBUS0, nBUS1, nBUS2, nBUS3, nBUS4, nBUS5, nBUS6,
       nBUS7, nBUS__gt_N, nC_1, nC_plus_1, nCLR, nCLR_PULSE, nCn_plus_8, nD_eq_0, nDE_IN, nDE_nOUT, nDEIN,
       nDEOUT, nI0, nI1, nI2, nI3, nI3_COND_eq_1, nI3I4RESTORE, nI4, nI5, nI6, nI6_NBIT3, nI7, nI8, nI9, nIA,
       nIABC, nIB, nIC, nID, nIE, nIF, nINREQUEST, nINTREG, nMANUAL, nN_0_8, nN_1_9, nN_2_A, nN_3_B, nN_4_C,
       nN_6_E, nN_7_F, nor_1_out, nor_18_out, nor_19_out, nor_20_out, nor_21_out, nor_24_out, not_1_out,
       not_3_out, not_4_out, not_5_out, not_6_out, not_11_out, not_12_out, nOUTREQUEST, nPX__gt_T, nRESTORE,
       nRESUME, nRSH, nRSL, nRWR, nS0, nS1, nS2, nS3, nSAVE, nT0, nT1, nT2, nT3, nT3_nT4_nRESTORE, nT4, nT5,
       nT6, nT7, nTP0, nTP2, nTP4, nTP5, nTP6, nTP7, nWE, O0, O1, O2, O3, O4, O5, O6, O7, O8, O10, O11, O12,
       O14, O15, P0, P1, P2, P3, P__gt_BUS, pullup_1_out, pullup_6_out, pullup_10_out, PX__gt_T, R0E, R1E,
       R__gt_A, RA0, RA1, RA2, RA3, RD_nWR, REPEAT, RES, RES_C, reset_1_out, RI0, RI1, RI2, RI3, RI4, RI5,
       RI6, RI7, RI8, RI9, RI10, RI11, RI12, RI13, RI14, RI15, S0, S1, S2, S3, SAVE, SEL_RN, SEL_RP, SEL_RX,
       SL, T0, T1, T2, T3, T4, T5, T6, T7, T__gt_B, T__gt_BUS, TP3, TP4, TP5, TP6, TP7, WI, WM, WP, WR, X0,
       X1, X2, X3;

  nand nand_1 (TP4, nRESTORE, nRESTORE);
  nand nand_2 (nand_2_out, nD_eq_0, nD_eq_0);
  nand nand_3 (nand_3_out, nTP7, nTP7);
  nand nand_4 (nand_4_out, nRESUME, nand_5_out);
  nand nand_5 (nand_5_out, nand_4_out, nTP0);
  not not_1 (not_1_out, nINREQUEST);
  Monoflop monoflop_1 (.C(TP7), .R(1'b0), .Q(monoflop_1_q));  // open: nQ
  nand nand_6 (nand_6_out, TP4, TP4);
  nand nand_7 (nand_7_out, nand_6_out, CLR_2);
  nand nand_8 (CLR_2, nand_7_out, nPX__gt_T);
  PullUp pullup_1 (.out(pullup_1_out));
  nand nand_9 (nand_9_out, nand_4_out, nOUTREQUEST);
  _74151 _74151_1 (
    .pin1(DF), .pin2(nand_2_out), .pin3(nD_eq_0), .pin4(pullup_1_out), .pin5(I3_COND_eq_1),
    .pin6(nI3_COND_eq_1), .pin7(nI3), .pin8(1'b0), .pin9(NBIT2), .pin10(NBIT1), .pin11(NBIT0),
    .pin12(_74151_1_pin12), .pin13(_74151_1_pin13), .pin14(_74151_1_pin14), .pin15(_74151_1_pin15),
    .pin16(1'b1));
  nor nor_1 (nor_1_out, nINTREG, nand_7_out);
  _7475 _7475_1 (
    .D0(nor_1_out), .Q0(INT_REG), .G1_2(monoflop_1_q), .D1(not_1_out), .Q1(_7475_1_q1), .D2(nand_9_out),
    .Q2(_7475_1_q2), .G3_4(monoflop_1_q), .nQ1(_7475_1_nq1), .nQ2(_7475_1_nq2), .VCC(1'b1), .GND(1'b0));  // open: D3, Q3, nQ0, nQ3
  PullUp pullup_2 (.out(EF4));
  PullUp pullup_3 (.out(EF2));
  PullUp pullup_4 (.out(EF3));
  PullUp pullup_5 (.out(EF1));
  _7475 _7475_2 (
    .D0(EF1), .G1_2(nand_3_out), .D1(EF2), .D2(EF3), .G3_4(nand_3_out), .D3(EF4), .nQ0(_74151_1_pin15),
    .nQ1(_74151_1_pin14), .nQ2(_74151_1_pin13), .nQ3(_74151_1_pin12), .VCC(1'b1), .GND(1'b0));  // open: Q0, Q1, Q2, Q3
  nand nand_10 (nDEIN, _7475_1_q1, S2);
  nand nand_11 (DE_REG, _7475_1_nq1, _7475_1_nq2);
  nand nand_12 (nDEOUT, _7475_1_q2, S2);
  // _62256 _62256_1: pin names not known; wires that end beside it: A14, A12, A7, A6, A5, A4, A3, A2, A1, A0, BUS0, BUS1, BUS2, 1'b0, 1'b1, nWE, A13, A8, A9, A11, A10, _62256_1_p22, BUS7
  // _28c256 _28c256_1: pin names not known; wires that end beside it: A14, A12, A7, A6, A5, A4, A3, A2, A1, A0, BUS0, BUS1, BUS2, 1'b0, 1'b1, A13, A8, A9, A11, A10, A15, BUS7
  not not_2 (_62256_1_p22, A15);
  nor nor_2 (RI15, C15, and_1_out);
  nor nor_3 (RI14, C14, and_2_out);
  _7401 _7401_1 (
    .pin1(nBUS7), .pin2(A1__gt_BUS), .pin3(A15), .pin4(nBUS6), .pin5(A1__gt_BUS), .pin6(A14), .pin7(1'b0),
    .pin8(A1__gt_BUS), .pin9(A13), .pin10(nBUS5), .pin11(A1__gt_BUS), .pin12(A12), .pin13(nBUS4), .pin14(1'b1));
  nor nor_4 (RI13, C13, and_3_out);
  _7475 _7475_3 (
    .D0(O15), .Q0(A15), .G1_2(R__gt_A), .D1(O14), .Q1(A14), .D2(nRSH), .Q2(A13), .G3_4(R__gt_A), .D3(O12),
    .Q3(A12), .VCC(1'b1), .GND(1'b0));  // open: nQ0, nQ1, nQ2, nQ3
  nor nor_5 (RI12, C12, and_4_out);
  nor nor_6 (RI11, C11, and_5_out);
  nor nor_7 (RI10, C10, and_6_out);
  _74193 _74193_1 (
    .pin1(A13), .pin2(C13), .pin3(C12), .pin4(_74193_1_pin4), .pin5(_74193_1_pin5), .pin6(C14), .pin7(C15),
    .pin8(1'b0), .pin9(A15), .pin10(A14), .pin11(nTP2), .pin14(RES_C), .pin15(A12), .pin16(1'b1));  // open: pin12, pin13
  nor nor_8 (RI9, C9, and_7_out);
  _7489 _7489_1 (
    .pin1(S0), .pin2(nRSH), .pin3(RD_nWR), .pin4(RI12), .pin5(O12), .pin6(RI13), .pin7(nRSH), .pin8(1'b0),
    .pin9(O14), .pin10(RI14), .pin11(O15), .pin12(RI15), .pin13(S3), .pin14(S2), .pin15(S1), .pin16(1'b1));
  nor nor_9 (RI8, C8, and_8_out);
  nor nor_10 (RI7, C7, and_1_out);
  and and_1 (and_1_out, BUS7, BUS__gt_R);
  _7401 _7401_2 (
    .pin1(nBUS3), .pin2(A1__gt_BUS), .pin3(A11), .pin4(nBUS2), .pin5(A1__gt_BUS), .pin6(A10), .pin7(1'b0),
    .pin8(A1__gt_BUS), .pin9(A9), .pin10(nBUS1), .pin11(A1__gt_BUS), .pin12(A8), .pin13(nBUS0), .pin14(1'b1));
  _7475 _7475_4 (
    .D0(O10), .Q0(A11), .G1_2(R__gt_A), .D1(O11), .Q1(A10), .D2(nRSH), .Q2(A9), .G3_4(R__gt_A), .D3(O8),
    .Q3(A8), .VCC(1'b1), .GND(1'b0));  // open: nQ0, nQ1, nQ2, nQ3
  nor nor_11 (RI6, C6, and_2_out);
  and and_2 (and_2_out, BUS6, BUS__gt_R);
  nor nor_12 (RI5, C5, and_3_out);
  and and_3 (and_3_out, BUS5, BUS__gt_R);
  nor nor_13 (RI4, C4, and_4_out);
  and and_4 (and_4_out, BUS4, BUS__gt_R);
  _74193 _74193_2 (
    .pin1(A9), .pin2(C9), .pin3(C8), .pin4(_74193_2_pin4), .pin5(_74193_2_pin5), .pin6(C10), .pin7(C11),
    .pin8(1'b0), .pin9(A11), .pin10(A10), .pin11(nTP2), .pin12(_74193_1_pin5), .pin13(_74193_1_pin4),
    .pin14(RES_C), .pin15(A8), .pin16(1'b1));
  nor nor_14 (RI3, C3, and_5_out);
  and and_5 (and_5_out, BUS3, BUS__gt_R);
  nor nor_15 (RI2, C2, and_6_out);
  and and_6 (and_6_out, BUS2, BUS__gt_R);
  _7489 _7489_2 (
    .pin1(S0), .pin2(nRSH), .pin3(RD_nWR), .pin4(RI8), .pin5(O8), .pin6(RI9), .pin7(nRSH), .pin8(1'b0),
    .pin9(O11), .pin10(RI10), .pin11(O10), .pin12(RI11), .pin13(S3), .pin14(S2), .pin15(S1), .pin16(1'b1));
  nor nor_16 (RI1, C1, and_7_out);
  and and_7 (and_7_out, BUS1, BUS__gt_R);
  _7401 _7401_3 (
    .pin1(nBUS7), .pin2(A0__gt_BUS), .pin3(A7), .pin4(nBUS6), .pin5(A0__gt_BUS), .pin6(A6), .pin7(1'b0),
    .pin8(A0__gt_BUS), .pin9(A5), .pin10(nBUS5), .pin11(A0__gt_BUS), .pin12(A4), .pin13(nBUS4), .pin14(1'b1));
  nor nor_17 (RI0, C0, and_8_out);
  and and_8 (and_8_out, BUS0, BUS__gt_R);
  _7475 _7475_5 (
    .D0(O7), .Q0(A7), .G1_2(R__gt_A), .D1(O6), .Q1(A6), .D2(O5), .Q2(A5), .G3_4(R__gt_A), .D3(O4), .Q3(A4),
    .VCC(1'b1), .GND(1'b0));  // open: nQ0, nQ1, nQ2, nQ3
  _74193 _74193_3 (
    .pin1(A5), .pin2(C5), .pin3(C4), .pin4(_74193_3_pin4), .pin5(_74193_3_pin5), .pin6(C6), .pin7(C7),
    .pin8(1'b0), .pin9(A7), .pin10(A6), .pin11(nTP2), .pin12(_74193_2_pin5), .pin13(_74193_2_pin4),
    .pin14(RES_C), .pin15(A4), .pin16(1'b1));
  _7489 _7489_3 (
    .pin1(S0), .pin2(nRSL), .pin3(RD_nWR), .pin4(RI4), .pin5(O4), .pin6(RI5), .pin7(O5), .pin8(1'b0),
    .pin9(O6), .pin10(RI6), .pin11(O7), .pin12(RI7), .pin13(S3), .pin14(S2), .pin15(S1), .pin16(1'b1));
  _7401 _7401_4 (
    .pin1(nBUS3), .pin2(A0__gt_BUS), .pin3(A3), .pin4(nBUS2), .pin5(A0__gt_BUS), .pin6(A2), .pin7(1'b0),
    .pin8(A0__gt_BUS), .pin9(A1), .pin10(nBUS1), .pin11(A0__gt_BUS), .pin12(A0), .pin13(nBUS0), .pin14(1'b1));
  _7475 _7475_6 (
    .D0(O3), .Q0(A3), .G1_2(R__gt_A), .D1(O2), .Q1(A2), .D2(O1), .Q2(A1), .G3_4(R__gt_A), .D3(O0), .Q3(A0),
    .VCC(1'b1), .GND(1'b0));  // open: nQ0, nQ1, nQ2, nQ3
  _74193 _74193_4 (
    .pin1(A1), .pin2(C1), .pin3(C0), .pin4(nC_1), .pin5(nC_plus_1), .pin6(C2), .pin7(C3), .pin8(1'b0),
    .pin9(A3), .pin10(A2), .pin11(nTP2), .pin12(_74193_3_pin5), .pin13(_74193_3_pin4), .pin14(RES_C),
    .pin15(A0), .pin16(1'b1));
  _7489 _7489_4 (
    .pin1(S0), .pin2(nRSL), .pin3(RD_nWR), .pin4(RI0), .pin5(O0), .pin6(RI1), .pin7(O1), .pin8(1'b0),
    .pin9(O2), .pin10(RI2), .pin11(O3), .pin12(RI3), .pin13(S3), .pin14(S2), .pin15(S1), .pin16(1'b1));
  nand nand_13 (nand_13_out, not_3_out, I0);
  nand nand_14 (nand_14_out, nand_16_out, nand_13_out);
  nand nand_15 (R__gt_A, nMANUAL, nand_14_out);
  not not_3 (not_3_out, SL);
  nand nand_16 (nand_16_out, I1, I1);
  nand nand_17 (nand_17_out, RUN, nand_18_out);
  nand nand_18 (nand_18_out, nand_17_out, clk);
  _7401 _7401_5 (
    .pin1(nBUS7), .pin2(T__gt_B), .pin3(_7401_5_pin3), .pin4(nBUS6), .pin5(T__gt_B), .pin6(_7401_5_pin6),
    .pin7(1'b0), .pin8(T__gt_B), .pin9(_7401_5_pin9), .pin10(nBUS5), .pin11(T__gt_B), .pin12(_7401_5_pin12),
    .pin13(nBUS4), .pin14(1'b1));
  _74173 _74173_1 (
    .pin1(1'b0), .pin2(1'b0), .pin3(X3), .pin4(X2), .pin5(X1), .pin6(X0), .pin7(PX__gt_T), .pin8(1'b0),
    .pin9(1'b0), .pin10(1'b0), .pin11(_7401_5_pin12), .pin12(_7401_5_pin9), .pin13(_7401_5_pin6),
    .pin14(_7401_5_pin3), .pin15(RES), .pin16(1'b1));
  Reset reset_1 (.out(reset_1_out));
  _74163 _74163_1 (
    .pin1(reset_1_out), .pin2(nand_18_out), .pin3(1'b0), .pin4(1'b0), .pin5(1'b0), .pin6(1'b0), .pin7(1'b1),
    .pin8(1'b0), .pin9(1'b1), .pin10(1'b1), .pin12(_74163_1_pin12), .pin13(_74163_1_pin13),
    .pin14(_74163_1_pin14), .pin16(1'b1));  // open: pin11, pin15
  PullUp pullup_6 (.out(pullup_6_out));
  PullUp pullup_7 (.out(pullup_6_out));
  _7401 _7401_6 (
    .pin1(_7401_6_pin1), .pin2(SEL_RX), .pin3(X3), .pin4(_7401_6_pin4), .pin5(SEL_RX), .pin6(X2),
    .pin7(1'b0), .pin8(SEL_RX), .pin9(X1), .pin10(pullup_6_out), .pin11(SEL_RX), .pin12(X0),
    .pin13(_7401_6_pin13), .pin14(1'b1));
  not not_4 (not_4_out, nCLR);
  PullUp pullup_8 (.out(pullup_6_out));
  PullUp pullup_9 (.out(_7401_6_pin13));
  _74173 _74173_2 (
    .pin1(1'b0), .pin2(1'b0), .pin3(BUS7), .pin4(BUS6), .pin5(BUS5), .pin6(BUS4), .pin8(1'b0), .pin9(1'b0),
    .pin10(BUS__gt_X), .pin11(X0), .pin12(X1), .pin13(X2), .pin14(X3), .pin15(1'b0), .pin16(1'b1));  // open: pin7
  _7401 _7401_7 (
    .pin1(nBUS3), .pin2(T__gt_B), .pin3(_7401_7_pin3), .pin4(nBUS2), .pin5(T__gt_B), .pin6(_7401_7_pin6),
    .pin7(1'b0), .pin8(T__gt_B), .pin9(_7401_7_pin9), .pin10(nBUS1), .pin11(T__gt_B), .pin12(_7401_7_pin12),
    .pin13(nBUS0), .pin14(1'b1));
  _74173 _74173_3 (
    .pin1(1'b0), .pin2(1'b0), .pin3(P3), .pin4(P2), .pin5(P1), .pin6(P0), .pin7(PX__gt_T), .pin8(1'b0),
    .pin9(1'b0), .pin10(1'b0), .pin11(_7401_7_pin12), .pin12(_7401_7_pin9), .pin13(_7401_7_pin6),
    .pin14(_7401_7_pin3), .pin15(RES), .pin16(1'b1));
  _74138 _74138_1 (
    .pin1(_74163_1_pin14), .pin2(_74163_1_pin13), .pin3(_74163_1_pin12), .pin4(1'b0), .pin5(1'b0),
    .pin6(1'b1), .pin7(nT7), .pin8(1'b0), .pin9(nT6), .pin10(nT5), .pin11(nT4), .pin12(nT3), .pin13(nT2),
    .pin14(nT1), .pin15(nT0), .pin16(1'b1));
  _7401 _7401_8 (
    .pin1(_7401_6_pin1), .pin2(SEL_RP), .pin3(P3), .pin4(_7401_6_pin4), .pin5(SEL_RP), .pin6(P2),
    .pin7(1'b0), .pin8(SEL_RP), .pin9(P1), .pin10(pullup_6_out), .pin11(SEL_RP), .pin12(P0),
    .pin13(_7401_6_pin13), .pin14(1'b1));
  _74173 _74173_4 (
    .pin1(1'b0), .pin2(1'b0), .pin3(BUS3), .pin4(BUS2), .pin5(BUS1), .pin6(BUS0), .pin8(1'b0), .pin9(1'b0),
    .pin10(BUS__gt_P), .pin11(P0), .pin12(P1), .pin13(P2), .pin14(P3), .pin15(not_4_out), .pin16(1'b1));  // open: pin7
  _7401 _7401_9 (
    .pin1(nBUS3), .pin2(in_7), .pin3(in_3), .pin4(nBUS2), .pin5(in_7), .pin6(in_4), .pin7(1'b0), .pin8(in_7),
    .pin9(in_5), .pin10(nBUS1), .pin11(in_7), .pin12(in_6), .pin13(nBUS0), .pin14(1'b1));
  _74540 _74540_1 (
    .pin1(1'b0), .pin2(nT0), .pin3(nT1), .pin4(nT2), .pin5(nT3), .pin6(nT4), .pin7(nT5), .pin8(nT6),
    .pin9(nT7), .pin10(1'b0), .pin11(T7), .pin12(T6), .pin13(T5), .pin14(T4), .pin15(T3), .pin16(T2),
    .pin17(T1), .pin18(T0), .pin19(1'b0), .pin20(1'b1));
  _7401 _7401_10 (
    .pin1(_7401_6_pin1), .pin2(SEL_RN), .pin3(N3), .pin4(_7401_6_pin4), .pin5(SEL_RN), .pin6(N2),
    .pin7(1'b0), .pin8(SEL_RN), .pin9(N1), .pin10(pullup_6_out), .pin11(SEL_RN), .pin12(N0),
    .pin13(_7401_6_pin13), .pin14(1'b1));
  _74173 _74173_5 (
    .pin1(1'b0), .pin2(1'b0), .pin3(BUS3), .pin4(BUS2), .pin5(BUS1), .pin6(BUS0), .pin8(1'b0), .pin9(1'b0),
    .pin10(BUS__gt_N), .pin11(N0), .pin12(N1), .pin13(N2), .pin14(N3), .pin15(not_4_out), .pin16(1'b1));  // open: pin7
  _74540 _74540_2 (
    .pin1(1'b0), .pin2(_7401_6_pin1), .pin3(_7401_6_pin4), .pin4(pullup_6_out), .pin5(_7401_6_pin13),
    .pin6(nN_6_E), .pin7(nN_2_A), .pin8(nN_1_9), .pin9(1'b0), .pin10(1'b0), .pin12(N_1_9), .pin13(N_2_A),
    .pin14(N_6_E), .pin15(RA0), .pin16(RA1), .pin17(RA2), .pin18(RA3), .pin19(1'b0), .pin20(1'b1));  // open: pin11
  _74138 _74138_2 (
    .pin1(N0), .pin2(N1), .pin3(N2), .pin4(INH_N), .pin5(1'b0), .pin6(1'b1), .pin7(nN_7_F), .pin8(1'b0),
    .pin9(nN_6_E), .pin10(Cn), .pin11(nN_4_C), .pin12(nN_3_B), .pin13(nN_2_A), .pin14(nN_1_9),
    .pin15(nN_0_8), .pin16(1'b1));
  not not_5 (not_5_out, DE_REG);
  not not_6 (not_6_out, INT_REG);
  nand nand_19 (nand_19_out, N_6_E, IF);
  _7401 _7401_11 (
    .pin1(nBUS7), .pin2(D__gt_BUS), .pin3(D_Bit_7), .pin4(nBUS6), .pin5(D__gt_BUS), .pin6(D_Bit_6),
    .pin7(1'b0), .pin8(D__gt_BUS), .pin9(D_Bit_5), .pin10(nBUS5), .pin11(D__gt_BUS), .pin12(D_Bit_4),
    .pin13(nBUS4), .pin14(1'b1));
  nand nand_20 (nand_20_out, S2, LOAD);
  nand nand_21 (nand_21_out, I0, not_5_out, not_6_out);
  nand nand_22 (nand_22_out, not_5_out, INT_REG, S1);
  nand nand_23 (nand_23_out, S1, DE_REG);
  _7495 _7495_1 (
    .Q0(D_Bit_7), .P0(F7), .S(nand_19_out), .nCP1(D_CLOCK), .nCP2(D_CLOCK), .Q1(D_Bit_6), .P1(F6),
    .Q2(D_Bit_5), .P2(F5), .Q3(D_Bit_4), .P3(F4), .VCC(1'b1), .GND(1'b0));  // open: DS
  nand nand_24 (nand_24_out, nand_20_out, nS0, nand_21_out, nand_22_out);
  nand nand_25 (nand_25_out, nand_22_out, nand_23_out);
  nor nor_18 (nor_18_out, D_Bit_0, D_Bit_1);
  nor nor_19 (nor_19_out, D_Bit_2, D_Bit_3);
  nor nor_20 (nor_20_out, D_Bit_4, D_Bit_5);
  nor nor_21 (nor_21_out, D_Bit_6, D_Bit_7);
  _74181 _74181_1 (
    .pin1(D_Bit_4), .pin2(BUS4), .pin3(S3), .pin4(S2), .pin5(S1), .pin6(S0), .pin7(_74181_1_pin7), .pin8(M),
    .pin9(F4), .pin10(F5), .pin11(F6), .pin12(1'b0));  // open: pin13, pin14, pin15, pin16, pin17, pin18, pin19, pin20, pin21, pin22, pin23, pin24
  _74181 _74181_2 (
    .pin1(D_Bit_0), .pin2(BUS0), .pin3(S3), .pin4(S2), .pin5(S1), .pin6(S0), .pin7(Cn), .pin8(M), .pin9(F0),
    .pin10(F1), .pin11(F2), .pin12(1'b0));  // open: pin13, pin14, pin15, pin16, pin17, pin18, pin19, pin20, pin21, pin22, pin23, pin24
  _7401 _7401_12 (
    .pin1(nBUS3), .pin2(D__gt_BUS), .pin3(D_Bit_3), .pin4(nBUS2), .pin5(D__gt_BUS), .pin6(D_Bit_2),
    .pin7(1'b0), .pin8(D__gt_BUS), .pin9(D_Bit_1), .pin10(nBUS1), .pin11(D__gt_BUS), .pin12(D_Bit_0),
    .pin13(nBUS0), .pin14(1'b1));
  nand nand_26 (nD_eq_0, nor_18_out, nor_19_out, nor_20_out, nor_21_out);
  _7474 _7474_1 (
    .pin1(nCLR), .pin2(nand_25_out), .pin3(_7474_1_pin3), .pin4(1'b1), .pin5(_7474_1_pin5),
    .pin6(_7474_1_pin6), .pin7(1'b0), .pin8(_7474_1_pin8), .pin9(_7474_1_pin9), .pin10(nCLR),
    .pin11(_7474_1_pin3), .pin12(nand_24_out), .pin13(1'b1), .pin14(1'b1));
  nand nand_27 (nS3, _7474_1_pin9, _7474_1_pin5);
  not not_7 (S3, nS3);
  _7495 _7495_2 (
    .Q0(D_Bit_3), .P0(F3), .S(nand_19_out), .DS(D_Bit_4), .nCP1(D_CLOCK), .nCP2(D_CLOCK), .Q1(D_Bit_2),
    .P1(F2), .Q2(D_Bit_1), .P2(F1), .Q3(D_Bit_0), .P3(F0), .VCC(1'b1), .GND(1'b0));
  nand nand_28 (nS2, _7474_1_pin8, _7474_1_pin5);
  not not_8 (S2, nS2);
  nand nand_29 (nS1, _7474_1_pin9, _7474_1_pin6);
  not not_9 (S1, nS1);
  nand nand_30 (nS0, _7474_1_pin8, _7474_1_pin6);
  nand nand_31 (S0, WI, nS0);
  nand nand_32 (_7474_1_pin3, TP7, REPEAT);
  nand nand_33 (nand_33_out, _7474_1_pin3, WI);
  nand nand_34 (nBUS__gt_N, nand_33_out, S0);
  _74175 _74175_1 (
    ._1Q(_74175_1__1q), ._1D(BUS0), ._2Q(_74175_1__2q), ._2D(BUS1), ._3Q(_74175_1__3q), ._3D(BUS2),
    ._4Q(_74175_1__4q), ._4D(BUS3), .VCC(1'b1), .GND(1'b0), .CLK(nBUS__gt_N), .nCLR(nCLR));  // open: n1Q, n2Q, n3Q, n4Q
  nand nand_35 (nand_35_out, Cn, nN_4_C);
  nand nand_36 (nCn_plus_8, Cn_plus_8, Cn_plus_8);
  nand nand_37 (nand_37_out, N_6_E, D_Bit_0);
  nand nand_38 (nand_38_out, TP5, IF);
  nand nand_39 (M, nN_3_B, nN_2_A, nN_1_9);
  nand nand_40 (S3, nN_4_C, nN_2_A, nN_1_9);
  nand nand_41 (S2, Cn, nN_3_B, nN_1_9);
  nand nand_42 (S1, Cn, nN_3_B, nN_2_A, nN_1_9);
  nand nand_43 (S0, nN_4_C, nN_2_A);
  nand nand_44 (nand_44_out, nand_35_out, Cn_plus_8);
  _74138 _74138_3 (
    .pin1(_74175_1__1q), .pin2(_74175_1__2q), .pin3(_74175_1__3q), .pin4(_74175_1__4q), .pin5(nS1),
    .pin6(1'b1), .pin7(nI7), .pin8(1'b0), .pin9(nI6), .pin10(nI5), .pin11(nI4), .pin12(nI3), .pin13(nI2),
    .pin14(nI1), .pin15(nI0), .pin16(1'b1));
  _74138 _74138_4 (
    .pin1(_74175_1__1q), .pin2(_74175_1__2q), .pin3(_74175_1__3q), .pin4(nS1), .pin5(1'b0),
    .pin6(_74175_1__4q), .pin7(nIF), .pin8(1'b0), .pin9(nIE), .pin10(nID), .pin11(nIC), .pin12(nIB),
    .pin13(nIA), .pin14(nI9), .pin15(nI8), .pin16(1'b1));
  nand nand_45 (nand_45_out, nand_44_out, nand_37_out);
  PullUp pullup_10 (.out(pullup_10_out));
  _7474 _7474_2 (
    .pin1(pullup_10_out), .pin2(nand_45_out), .pin3(nand_38_out), .pin4(pullup_10_out), .pin5(DF),
    .pin7(1'b0), .pin11(1'b0), .pin12(1'b0), .pin13(1'b0), .pin14(1'b1));  // open: pin6, pin8, pin9, pin10
  _74540 _74540_3 (
    .pin1(1'b0), .pin2(nBUS7), .pin3(nBUS6), .pin4(nBUS5), .pin5(nBUS4), .pin6(nBUS3), .pin7(nBUS2),
    .pin8(nBUS1), .pin9(nBUS0), .pin10(1'b0), .pin11(BUS0), .pin12(BUS1), .pin13(BUS2), .pin14(BUS3),
    .pin15(BUS4), .pin16(BUS5), .pin17(BUS6), .pin18(BUS7), .pin19(1'b0), .pin20(1'b1));
  _74540 _74540_4 (
    .pin1(1'b0), .pin2(nI0), .pin3(nI2), .pin4(nI4), .pin5(nI6), .pin6(nI7), .pin7(nI8), .pin8(nI9),
    .pin9(nIF), .pin10(1'b0), .pin11(IF), .pin12(I9), .pin13(I8), .pin14(I7), .pin15(I6), .pin16(I4),
    .pin17(I2), .pin18(I0), .pin19(1'b0), .pin20(1'b1));
  nand nand_46 (nand_46_out, nIA, nIB, nIC);
  not not_10 (nIABC, nand_46_out);
  nand nand_47 (nI6_NBIT3, I6, NBIT3);
  nand nand_48 (T__gt_BUS, SAVE, SAVE);
  nand nand_49 (P__gt_BUS, nID, nIE);
  nand nand_50 (N__gt_BUS, nI5, nIABC);
  nand nand_51 (A1__gt_BUS, nI9, nI9);
  nand nand_52 (A0__gt_BUS, nIB, nIB);
  nand nand_53 (INH_N_DECODE, nI9, nIB, nI4);
  nand nand_54 (nand_54_out, I7, NBIT3);
  nand nand_55 (nand_55_out, nTP5, nand_56_out);
  nand nand_56 (nand_56_out, nand_55_out, nTP7);
  nand nand_57 (BUS__gt_R, nIABC, nMANUAL, nI3_COND_eq_1);
  nand nand_58 (nand_58_out, nI3, nI4);
  nand nand_59 (SEL_RP, nI3, nS0);
  nand nand_60 (SEL_RX, nI6, nI7, nIF);
  nand nand_61 (nand_61_out, nTP4, nand_62_out);
  nand nand_62 (nand_62_out, nand_61_out, nTP6);
  nand nand_63 (nSAVE, I7, NBIT3);
  nand nand_64 (nand_64_out, NBIT3, nI6);
  nand nand_65 (nPX__gt_T, TP4, S3);
  nand nand_66 (M__gt_BUS, nT3_nT4_nRESTORE, nI0, nIF, nS0, nDE_nOUT, nI6_NBIT3);
  not not_11 (not_11_out, INH_N_DECODE);
  and and_9 (and_9_out, nS3, nand_54_out);
  nand nand_67 (nand_67_out, nand_55_out, I3_COND_eq_1);
  nor nor_22 (SEL_RN, SEL_RP, S2, SEL_RX);
  nand nand_68 (nand_68_out, not_11_out, nIF);
  nor nor_23 (nI3I4RESTORE, TP4, nand_58_out);
  nand nand_69 (nand_69_out, nSAVE, nand_64_out, nI5, nDE_IN);
  nand nand_70 (nand_70_out, nID, and_9_out);
  nand nand_71 (nand_71_out, and_9_out, nIE);
  and and_10 (D_CLOCK, nand_68_out, TP6);
  nand nand_72 (INH_R10, nand_67_out, nIA, R0E, nIC);
  nand nand_73 (INH_R01, nIC, nIB, R1E);
  nand nand_74 (INH_R00, R1E, nIB);
  nand nand_75 (nand_75_out, nand_61_out, nand_69_out);
  nand nand_76 (nand_76_out, TP7, nand_70_out);
  and and_11 (BUS__gt_X, nand_71_out, TP7);
  nand nand_77 (nand_77_out, nI6_NBIT3, nI1, S1, nI3I4RESTORE);
  and and_12 (nWE, WM, nand_75_out);
  nand nand_78 (BUS__gt_P, WP, nand_76_out);
  nor nor_24 (nor_24_out, I2, nand_77_out, BUS__gt_R);
  nand nand_79 (nand_79_out, BUS__gt_R, TP3);
  nand nand_80 (nC_plus_1, nI3_COND_eq_1, TP3, nand_77_out);
  nand nand_81 (nC_1, TP3, I2);
  not not_12 (not_12_out, nor_24_out);
  nand nand_82 (nand_82_out, TP6, not_12_out);
  nand nand_83 (nand_83_out, WR, nCLR_PULSE, nand_82_out);
  nand nand_84 (RES_C, nCLR_PULSE, nand_79_out);
  nand nand_85 (nRWR, nS3, nand_83_out);

  // Other names for the same wires on the sheet: INH_R11 = INH_R10; nN_5_D = Cn; O9 = nRSH; O13 = nRSH

  // Notes on the sheet:
  //   clk: Hz: 100
  //   LOGIC 7 External Interface
  //   LOGIC 3 Memory
  //   3  7400
  //   2   7475
  //   1   74151
  //   1   7402
  //   Total 7
  //   LOGIC 8 Channel Control
  //   LOGIC 4 Register Stack
  //   A->C
  //   16 x 16-BIT RAM
  //   U/D COUNTER
  //   1  7400
  //   4   7401
  //   4  7402
  //   2  7408
  //   4  7475
  //   4  7489
  //   4  74193
  //   Total  23
  //   LOGIC 9 Timing Generator
  //   LOGIC 5 P-X-N-T
  //   REG TH
  //   REG X
  //   REG TL
  //   REG P
  //   REG N
  //   6  7401
  //   1  74138
  //   5  74173
  //   1  74540
  //   Total 13
  //   1  7400
  //   1  74138
  //   1  74163
  //   1  74540
  //   Total 4
  //   LOGIC 10 I, S Decode
  //   LOGIC 6 D Register, ALU
  //   AND
  //   OR
  //   XOR
  //   ADD
  //   SUB
  //   3  7400
  //   1  7404
  //   1  7410
  //   1  7420
  //   1  7474
  //   1  74175
  //   2  74138
  //   1  74540
  //   Total 11
  //   2  7400
  //   2  7401
  //   1  7402
  //   1  7410
  //   1  7420
  //   1  7474
  //   2   7495
  //   2   74181
  //   1  74540
  //   Total 8
  //   LOGIC 11 Bus Select
  //   LOGIC 12 R-C Control
  //   LOGIC 13 M-D-MSC Control
  //   Memory Write
  //   1  7408
  //   1  7430
  //   3  7400
  //   Total 5
  //   3  7400
  //   2   7410
  //   1  7420
  //   1  7427
  //   Total 7
  //   2  7400
  //   1  7420
  //   1  7408
  //   Total 4
endmodule
