// Digital circuit JAWS_Top_Level_3.dig as structural Verilog
module JAWS_Top_Level_3 (
  input  clk,
  input  RUN,
  input  in_3,
  input  in_4,
  input  in_5,
  input  in_6,
  input  in_7,
  input  in_8,
  input  in_9,
  input  in_10,
  input  in_11,
  input  in_12,
  input  in_13,
  input  in_14,
  input  in_15,
  input  in_16,
  input  in_17,
  input  in_18,
  input  in_19,
  input  in_20,
  input  in_21,
  input  in_22,
  input  in_23,
  input  in_24,
  input  in_25,
  input  nRESET
);

  wire _7401_5_pin3, _7401_5_pin6, _7401_5_pin9, _7401_5_pin12, _7401_6_pin10, _7401_6_pin13, _7401_7_pin3,
       _7401_7_pin6, _7401_7_pin9, _7401_7_pin12, _7474_1_pin3, _7474_1_pin5, _7474_1_pin6, _7474_1_pin8,
       _7474_1_pin9, _7475_1_nq1, _7475_1_nq2, _7475_1_q1, _7475_1_q2, _62256_1_p23, _74151_1_pin12,
       _74151_1_pin13, _74151_1_pin14, _74151_1_pin15, _74163_1_pin12, _74163_1_pin13, _74163_1_pin14,
       _74181_1_pin7, _74193_1_pin4, _74193_1_pin5, _74193_2_pin4, _74193_2_pin5, _74193_3_pin4,
       _74193_3_pin5, A0, A0__gt_BUS, A1, A1__gt_BUS, A2, A3, A4, A5, A6, A7, A8, A9, A10, A11, A12, A13,
       A14, A15, and_1_out, and_2_out, and_3_out, and_4_out, and_5_out, and_6_out, and_7_out, and_8_out,
       and_9_out, AS0, AS1, AS2, AS3, BUS0, BUS1, BUS2, BUS3, BUS4, BUS5, BUS6, BUS7, BUS__gt_P, BUS__gt_R,
       BUS__gt_X, C0, C1, C2, C3, C4, C5, C6, C7, C8, C9, C10, C11, C12, C13, C14, C15, CLR, CLR_2, Cn,
       Cn_plus_8, D__gt_BUS, D_Bit_0, D_Bit_1, D_Bit_2, D_Bit_3, D_Bit_4, D_Bit_5, D_Bit_6, D_Bit_7, D_CLOCK,
       DE_REG, DF, F0, F1, F2, F3, F4, F5, F6, F7, I0, I2, I3_COND_eq_1, I4, I6, I7, I8, I9, IF, INH_N,
       INH_N_DECODE, INH_R00, INH_R01, INH_R10, INT_REG, M, M__gt_BUS, monoflop_1_q, N0, N1, N2, N3, N_1_9,
       N_2_A, N_6_E, N__gt_BUS, nand_2_out, nand_3_out, nand_4_out, nand_5_out, nand_6_out, nand_7_out,
       nand_9_out, nand_13_out, nand_14_out, nand_16_out, nand_17_out, nand_18_out, nand_20_out, nand_21_out,
       nand_22_out, nand_23_out, nand_24_out, nand_25_out, nand_26_out, nand_34_out, nand_36_out,
       nand_38_out, nand_39_out, nand_45_out, nand_46_out, nand_47_out, nand_55_out, nand_56_out,
       nand_57_out, nand_59_out, nand_62_out, nand_63_out, nand_65_out, nand_68_out, nand_69_out,
       nand_70_out, nand_71_out, nand_72_out, nand_76_out, nand_77_out, nand_78_out, nand_80_out,
       nand_83_out, nand_84_out, NBIT3, nBUS0, nBUS1, nBUS2, nBUS3, nBUS4, nBUS5, nBUS6, nBUS7, nBUS__gt_N,
       nC_1, nC_plus_1, nCn_plus_8, nD_eq_0, nDEIN, nDEOUT, nI0, nI1, nI2, nI3, nI3_COND_eq_1, nI3I4RESTORE,
       nI4, nI5, nI6, nI6_NBIT3, nI7, nI8, nI9, nIA, nIABC, nIB, nIC, nID, nIE, nIF, nMANUAL, nN_0_8, nN_1_9,
       nN_2_A, nN_3_B, nN_4_C, nN_6_E, nN_7_F, nNBIT3, nor_1_out, nor_18_out, nor_19_out, nor_20_out,
       nor_21_out, nor_24_out, not_18_out, not_20_out, not_21_out, not_24_out, not_25_out, not_30_out,
       not_32_out, nPX__gt_T, nRESTORE, nRWR, nS0, nS1, nS2, nS3, nT0, nT1, nT2, nT3, nT4, nT5, nT6, nT7,
       nWE, O0, O1, O2, O3, O4, O5, O6, O7, O8, O9, O10, O11, O12, O13, O14, O15, OP0, OP1, OP2, OP3, P0, P1,
       P2, P3, pullup_13_out, pullup_19_out, pullup_20_out, pullup_27_out, PX__gt_T, R__gt_A, RA0, RA1, RA2,
       RA3, RES_C, RESTORE, RI0, RI1, RI2, RI3, RI4, RI5, RI6, RI7, RI8, RI9, RI10, RI11, RI12, RI13, RI14,
       RI15, S0, S1, S2, S3, SEL_RN, SEL_RP, SEL_RX, SL, T0, T1, T2, T3, T4, T5, T6, T7, T__gt_BUS, X0, X1,
       X2, X3;
  wire [3:0] not_1_out, not_5_out, not_9_out, not_13_out;

  Seven_Seg_Hex seven_seg_hex_1 (.d({A15, A14, A13, A12}), .dp(1'b0));
  Seven_Seg_Hex seven_seg_hex_2 (.d({A11, A10, A9, A8}), .dp(1'b0));
  Seven_Seg_Hex seven_seg_hex_3 (.d({A7, A6, A5, A4}), .dp(1'b0));
  Seven_Seg_Hex seven_seg_hex_4 (.d({OP3, OP2, OP1, OP0}), .dp(1'b0));
  Seven_Seg_Hex seven_seg_hex_5 (.d({A3, A2, A1, A0}), .dp(1'b0));
  Seven_Seg_Hex seven_seg_hex_6 (.d({N3, N2, N1, N0}), .dp(1'b0));
  Seven_Seg_Hex seven_seg_hex_7 (.d({X3, X2, X1, X0}), .dp(1'b0));
  Seven_Seg_Hex seven_seg_hex_8 (.d({BUS7, BUS6, BUS5, BUS4}), .dp(1'b0));
  Seven_Seg_Hex seven_seg_hex_9 (.d({P3, P2, P1, P0}), .dp(1'b0));
  Seven_Seg_Hex seven_seg_hex_10 (.d({BUS3, BUS2, BUS1, BUS0}), .dp(1'b0));
  Seven_Seg_Hex seven_seg_hex_11 (.d({RA3, RA2, RA1, RA0}), .dp(1'b0));
  Seven_Seg_Hex seven_seg_hex_12 (.d({C15, C14, C13, C12}), .dp(1'b0));
  Seven_Seg_Hex seven_seg_hex_13 (.d({C11, C10, C9, C8}), .dp(1'b0));
  Seven_Seg_Hex seven_seg_hex_14 (.d({C7, C6, C5, C4}), .dp(1'b0));
  Seven_Seg_Hex seven_seg_hex_15 (.d({C3, C2, C1, C0}), .dp(1'b0));
  not not_1 (not_1_out[3], O15);
  not not_2 (not_1_out[2], O14);
  not not_3 (not_1_out[1], O13);
  not not_4 (not_1_out[0], O12);
  not not_5 (not_5_out[3], O10);
  not not_6 (not_5_out[2], O11);
  not not_7 (not_5_out[1], O9);
  not not_8 (not_5_out[0], O8);
  not not_9 (not_9_out[3], O7);
  not not_10 (not_9_out[2], O6);
  not not_11 (not_9_out[1], O5);
  not not_12 (not_9_out[0], O4);
  not not_13 (not_13_out[3], O3);
  not not_14 (not_13_out[2], O2);
  not not_15 (not_13_out[1], O1);
  not not_16 (not_13_out[0], O0);
  Seven_Seg_Hex seven_seg_hex_16 (.d(not_1_out), .dp(1'b0));
  Seven_Seg_Hex seven_seg_hex_17 (.d(not_5_out), .dp(1'b0));
  Seven_Seg_Hex seven_seg_hex_18 (.d(not_9_out), .dp(1'b0));
  Seven_Seg_Hex seven_seg_hex_19 (.d(not_13_out), .dp(1'b0));
  Seven_Seg_Hex seven_seg_hex_20 (.d({RI15, RI14, RI13, RI12}), .dp(1'b0));
  PullUp pullup_1 (.out(in_23));
  Seven_Seg_Hex seven_seg_hex_21 (.d({RI11, RI10, RI9, RI8}), .dp(1'b0));
  PullUp pullup_2 (.out(in_22));
  PullUp pullup_3 (.out(in_24));
  Seven_Seg_Hex seven_seg_hex_22 (.d({RI7, RI6, RI5, RI4}), .dp(1'b0));
  PullUp pullup_4 (.out(in_20));
  PullUp pullup_5 (.out(in_21));
  Seven_Seg_Hex seven_seg_hex_23 (.d({RI3, RI2, RI1, RI0}), .dp(1'b0));
  LED led_1 (.in(T7));
  LED led_2 (.in(T6));
  LED led_3 (.in(T5));
  LED led_4 (.in(T4));
  LED led_5 (.in(T3));
  LED led_6 (.in(T2));
  LED led_7 (.in(T1));
  LED led_8 (.in(T0));
  PullUp pullup_6 (.out(in_18));
  PullUp pullup_7 (.out(in_19));
  PullUp pullup_8 (.out(in_9));
  PullUp pullup_9 (.out(in_16));
  PullUp pullup_10 (.out(in_17));
  not not_17 (nMANUAL, in_22);
  PullUp pullup_11 (.out(in_8));
  PullUp pullup_12 (.out(in_14));
  nand nand_1 (RESTORE, nRESTORE, nRESTORE);
  nand nand_2 (nand_2_out, nD_eq_0, nD_eq_0);
  nand nand_3 (nand_3_out, nT7, nT7);
  nand nand_4 (nand_4_out, in_15, nand_5_out);
  nand nand_5 (nand_5_out, nand_4_out, nT0);
  not not_18 (not_18_out, in_8);
  Monoflop monoflop_1 (.C(T7), .R(1'b0), .Q(monoflop_1_q));  // open: nQ
  nand nand_6 (nand_6_out, RESTORE, T4);
  nand nand_7 (nand_7_out, nand_6_out, CLR_2);
  nand nand_8 (CLR_2, nand_7_out, nPX__gt_T);
  PullUp pullup_13 (.out(pullup_13_out));
  nand nand_9 (nand_9_out, nand_4_out, in_9);
  _74151 _74151_1 (
    .pin1(DF), .pin2(nand_2_out), .pin3(nD_eq_0), .pin4(pullup_13_out), .pin5(I3_COND_eq_1),
    .pin6(nI3_COND_eq_1), .pin7(nI3), .pin8(1'b0), .pin9(N2), .pin10(N1), .pin11(N0), .pin12(_74151_1_pin12),
    .pin13(_74151_1_pin13), .pin14(_74151_1_pin14), .pin15(_74151_1_pin15), .pin16(1'b1));
  nor nor_1 (nor_1_out, in_14, nand_7_out);
  _7475 _7475_1 (
    .D0(nor_1_out), .Q0(INT_REG), .G1_2(monoflop_1_q), .D1(not_18_out), .Q1(_7475_1_q1), .D2(nand_9_out),
    .Q2(_7475_1_q2), .G3_4(monoflop_1_q), .D3(1'b0), .nQ1(_7475_1_nq1), .nQ2(_7475_1_nq2), .VCC(1'b1),
    .GND(1'b0));  // open: Q3, nQ0, nQ3
  PullUp pullup_14 (.out(in_10));
  PullUp pullup_15 (.out(in_12));
  PullUp pullup_16 (.out(in_11));
  PullUp pullup_17 (.out(in_13));
  _7475 _7475_2 (
    .D0(in_13), .G1_2(nand_3_out), .D1(in_12), .D2(in_11), .G3_4(nand_3_out), .D3(in_10),
    .nQ0(_74151_1_pin15), .nQ1(_74151_1_pin14), .nQ2(_74151_1_pin13), .nQ3(_74151_1_pin12), .VCC(1'b1),
    .GND(1'b0));  // open: Q0, Q1, Q2, Q3
  nand nand_10 (nDEIN, _7475_1_q1, S2);
  nand nand_11 (DE_REG, _7475_1_nq1, _7475_1_nq2);
  nand nand_12 (nDEOUT, _7475_1_q2, S2);
  // _62256 _62256_1: pin names not known; wires that end beside it: A14, A12, A7, A6, A5, A4, A3, A2, A1, A0, BUS0, BUS1, BUS2, 1'b0, 1'b1, nWE, A13, A8, A9, A11, 1'b0, A10, _62256_1_p23, BUS7
  // _28c256 _28c256_1: pin names not known; wires that end beside it: A14, A12, A7, A6, A5, A4, A3, A2, A1, A0, BUS0, BUS1, BUS2, 1'b0, 1'b1, 1'b1, A13, A8, A9, A11, 1'b0, A10, A15, BUS7
  not not_19 (_62256_1_p23, A15);
  nor nor_2 (RI15, C15, and_1_out);
  nor nor_3 (RI14, C14, and_2_out);
  _7401 _7401_1 (
    .pin1(nBUS7), .pin2(A1__gt_BUS), .pin3(A15), .pin4(nBUS6), .pin5(A1__gt_BUS), .pin6(A14), .pin7(1'b0),
    .pin8(A1__gt_BUS), .pin9(A13), .pin10(nBUS5), .pin11(A1__gt_BUS), .pin12(A12), .pin13(nBUS4), .pin14(1'b1));
  nor nor_4 (RI13, C13, and_3_out);
  _7475 _7475_3 (
    .D0(O15), .Q0(A15), .G1_2(R__gt_A), .D1(O14), .Q1(A14), .D2(O13), .Q2(A13), .G3_4(R__gt_A), .D3(O12),
    .Q3(A12), .VCC(1'b1), .GND(1'b0));  // open: nQ0, nQ1, nQ2, nQ3
  nor nor_5 (RI12, C12, and_4_out);
  nor nor_6 (RI11, C11, and_5_out);
  nor nor_7 (RI10, C10, and_6_out);
  _74193 _74193_1 (
    .pin1(A13), .pin2(C13), .pin3(C12), .pin4(_74193_1_pin4), .pin5(_74193_1_pin5), .pin6(C14), .pin7(C15),
    .pin8(1'b0), .pin9(A15), .pin10(A14), .pin11(nT2), .pin14(RES_C), .pin15(A12), .pin16(1'b1));  // open: pin12, pin13
  nor nor_8 (RI9, C9, and_7_out);
  _7489 _7489_1 (
    .pin1(RA0), .pin2(INH_R10), .pin3(nRWR), .pin4(RI12), .pin5(O12), .pin6(RI13), .pin7(O13), .pin8(1'b0),
    .pin9(O14), .pin10(RI14), .pin11(O15), .pin12(RI15), .pin13(RA3), .pin14(RA2), .pin15(RA1), .pin16(1'b1));
  nor nor_9 (RI8, C8, and_8_out);
  nor nor_10 (RI7, C7, and_1_out);
  and and_1 (and_1_out, BUS7, BUS__gt_R);
  _7401 _7401_2 (
    .pin1(nBUS3), .pin2(A1__gt_BUS), .pin3(A11), .pin4(nBUS2), .pin5(A1__gt_BUS), .pin6(A10), .pin7(1'b0),
    .pin8(A1__gt_BUS), .pin9(A9), .pin10(nBUS1), .pin11(A1__gt_BUS), .pin12(A8), .pin13(nBUS0), .pin14(1'b1));
  _7475 _7475_4 (
    .D0(O10), .Q0(A11), .G1_2(R__gt_A), .D1(O11), .Q1(A10), .D2(O9), .Q2(A9), .G3_4(R__gt_A), .D3(O8),
    .Q3(A8), .VCC(1'b1), .GND(1'b0));  // open: nQ0, nQ1, nQ2, nQ3
  nor nor_11 (RI6, C6, and_2_out);
  and and_2 (and_2_out, BUS6, BUS__gt_R);
  nor nor_12 (RI5, C5, and_3_out);
  and and_3 (and_3_out, BUS5, BUS__gt_R);
  nor nor_13 (RI4, C4, and_4_out);
  and and_4 (and_4_out, BUS4, BUS__gt_R);
  _74193 _74193_2 (
    .pin1(A9), .pin2(C9), .pin3(C8), .pin4(_74193_2_pin4), .pin5(_74193_2_pin5), .pin6(C10), .pin7(C11),
    .pin8(1'b0), .pin9(A11), .pin10(A10), .pin11(nT2), .pin12(_74193_1_pin5), .pin13(_74193_1_pin4),
    .pin14(RES_C), .pin15(A8), .pin16(1'b1));
  nor nor_14 (RI3, C3, and_5_out);
  and and_5 (and_5_out, BUS3, BUS__gt_R);
  nor nor_15 (RI2, C2, and_6_out);
  and and_6 (and_6_out, BUS2, BUS__gt_R);
  _7489 _7489_2 (
    .pin1(RA0), .pin2(INH_R10), .pin3(nRWR), .pin4(RI8), .pin5(O8), .pin6(RI9), .pin7(O9), .pin8(1'b0),
    .pin9(O11), .pin10(RI10), .pin11(O10), .pin12(RI11), .pin13(RA3), .pin14(RA2), .pin15(RA1), .pin16(1'b1));
  nor nor_16 (RI1, C1, and_7_out);
  and and_7 (and_7_out, BUS1, BUS__gt_R);
  _7401 _7401_3 (
    .pin1(nBUS7), .pin2(A0__gt_BUS), .pin3(A7), .pin4(nBUS6), .pin5(A0__gt_BUS), .pin6(A6), .pin7(1'b0),
    .pin8(A0__gt_BUS), .pin9(A5), .pin10(nBUS5), .pin11(A0__gt_BUS), .pin12(A4), .pin13(nBUS4), .pin14(1'b1));
  nor nor_17 (RI0, C0, and_8_out);
  and and_8 (and_8_out, BUS0, BUS__gt_R);
  _7475 _7475_5 (
    .D0(O7), .Q0(A7), .G1_2(R__gt_A), .D1(O6), .Q1(A6), .D2(O5), .Q2(A5), .G3_4(R__gt_A), .D3(O4), .Q3(A4),
    .VCC(1'b1), .GND(1'b0));  // open: nQ0, nQ1, nQ2, nQ3
  _74193 _74193_3 (
    .pin1(A5), .pin2(C5), .pin3(C4), .pin4(_74193_3_pin4), .pin5(_74193_3_pin5), .pin6(C6), .pin7(C7),
    .pin8(1'b0), .pin9(A7), .pin10(A6), .pin11(nT2), .pin12(_74193_2_pin5), .pin13(_74193_2_pin4),
    .pin14(RES_C), .pin15(A4), .pin16(1'b1));
  _7489 _7489_3 (
    .pin1(RA0), .pin2(INH_R01), .pin3(nRWR), .pin4(RI4), .pin5(O4), .pin6(RI5), .pin7(O5), .pin8(1'b0),
    .pin9(O6), .pin10(RI6), .pin11(O7), .pin12(RI7), .pin13(RA3), .pin14(RA2), .pin15(RA1), .pin16(1'b1));
  _7401 _7401_4 (
    .pin1(nBUS3), .pin2(A0__gt_BUS), .pin3(A3), .pin4(nBUS2), .pin5(A0__gt_BUS), .pin6(A2), .pin7(1'b0),
    .pin8(A0__gt_BUS), .pin9(A1), .pin10(nBUS1), .pin11(A0__gt_BUS), .pin12(A0), .pin13(nBUS0), .pin14(1'b1));
  _7475 _7475_6 (
    .D0(O3), .Q0(A3), .G1_2(R__gt_A), .D1(O2), .Q1(A2), .D2(O1), .Q2(A1), .G3_4(R__gt_A), .D3(O0), .Q3(A0),
    .VCC(1'b1), .GND(1'b0));  // open: nQ0, nQ1, nQ2, nQ3
  _74193 _74193_4 (
    .pin1(A1), .pin2(C1), .pin3(C0), .pin4(nC_1), .pin5(nC_plus_1), .pin6(C2), .pin7(C3), .pin8(1'b0),
    .pin9(A3), .pin10(A2), .pin11(nT2), .pin12(_74193_3_pin5), .pin13(_74193_3_pin4), .pin14(RES_C),
    .pin15(A0), .pin16(1'b1));
  _7489 _7489_4 (
    .pin1(RA0), .pin2(INH_R00), .pin3(nRWR), .pin4(RI0), .pin5(O0), .pin6(RI1), .pin7(O1), .pin8(1'b0),
    .pin9(O2), .pin10(RI2), .pin11(O3), .pin12(RI3), .pin13(RA3), .pin14(RA2), .pin15(RA1), .pin16(1'b1));
  PullUp pullup_18 (.out(SL));
  nand nand_13 (nand_13_out, not_20_out, I0);
  nand nand_14 (nand_14_out, nand_16_out, nand_13_out);
  nand nand_15 (R__gt_A, nMANUAL, nand_14_out);
  not not_20 (not_20_out, SL);
  nand nand_16 (nand_16_out, nI1, nI1);
  not not_21 (not_21_out, PX__gt_T);
  nand nand_17 (nand_17_out, RUN, nand_18_out);
  nand nand_18 (nand_18_out, nand_17_out, clk);
  _7401 _7401_5 (
    .pin1(nBUS7), .pin2(T__gt_BUS), .pin3(_7401_5_pin3), .pin4(nBUS6), .pin5(T__gt_BUS), .pin6(_7401_5_pin6),
    .pin7(1'b0), .pin8(T__gt_BUS), .pin9(_7401_5_pin9), .pin10(nBUS5), .pin11(T__gt_BUS),
    .pin12(_7401_5_pin12), .pin13(nBUS4), .pin14(1'b1));
  _7475 _7475_7 (
    .D0(X3), .Q0(_7401_5_pin3), .G1_2(not_21_out), .D1(X2), .Q1(_7401_5_pin6), .D2(X1), .Q2(_7401_5_pin9),
    .G3_4(not_21_out), .D3(X0), .Q3(_7401_5_pin12), .VCC(1'b1), .GND(1'b0));  // open: nQ0, nQ1, nQ2, nQ3
  not not_22 (CLR, nRESET);
  _74163 _74163_1 (
    .pin1(nRESET), .pin2(nand_18_out), .pin3(1'b0), .pin4(1'b0), .pin5(1'b0), .pin6(1'b0), .pin7(1'b1),
    .pin8(1'b0), .pin9(1'b1), .pin10(1'b1), .pin12(_74163_1_pin12), .pin13(_74163_1_pin13),
    .pin14(_74163_1_pin14), .pin16(1'b1));  // open: pin11, pin15
  PullUp pullup_19 (.out(pullup_19_out));
  PullUp pullup_20 (.out(pullup_20_out));
  _7401 _7401_6 (
    .pin1(pullup_19_out), .pin2(SEL_RX), .pin3(X3), .pin4(pullup_20_out), .pin5(SEL_RX), .pin6(X2),
    .pin7(1'b0), .pin8(SEL_RX), .pin9(X1), .pin10(_7401_6_pin10), .pin11(SEL_RX), .pin12(X0),
    .pin13(_7401_6_pin13), .pin14(1'b1));
  PullUp pullup_21 (.out(_7401_6_pin10));
  PullUp pullup_22 (.out(_7401_6_pin13));
  _7475 _7475_8 (
    .D0(BUS7), .Q0(X3), .G1_2(BUS__gt_X), .D1(BUS6), .Q1(X2), .D2(BUS5), .Q2(X1), .G3_4(BUS__gt_X),
    .D3(BUS4), .Q3(X0), .VCC(1'b1), .GND(1'b0));  // open: nQ0, nQ1, nQ2, nQ3
  _7401 _7401_7 (
    .pin1(nBUS3), .pin2(T__gt_BUS), .pin3(_7401_7_pin3), .pin4(nBUS2), .pin5(T__gt_BUS), .pin6(_7401_7_pin6),
    .pin7(1'b0), .pin8(T__gt_BUS), .pin9(_7401_7_pin9), .pin10(nBUS1), .pin11(T__gt_BUS),
    .pin12(_7401_7_pin12), .pin13(nBUS0), .pin14(1'b1));
  _7475 _7475_9 (
    .D0(P3), .Q0(_7401_7_pin3), .G1_2(not_21_out), .D1(P2), .Q1(_7401_7_pin6), .D2(P1), .Q2(_7401_7_pin9),
    .G3_4(not_21_out), .D3(P0), .Q3(_7401_7_pin12), .VCC(1'b1), .GND(1'b0));  // open: nQ0, nQ1, nQ2, nQ3
  _74138 _74138_1 (
    .pin1(_74163_1_pin14), .pin2(_74163_1_pin13), .pin3(_74163_1_pin12), .pin4(1'b0), .pin5(1'b0),
    .pin6(1'b1), .pin7(nT7), .pin8(1'b0), .pin9(nT6), .pin10(nT5), .pin11(nT4), .pin12(nT3), .pin13(nT2),
    .pin14(nT1), .pin15(nT0), .pin16(1'b1));
  _7401 _7401_8 (
    .pin1(pullup_19_out), .pin2(SEL_RP), .pin3(P3), .pin4(pullup_20_out), .pin5(SEL_RP), .pin6(P2),
    .pin7(1'b0), .pin8(SEL_RP), .pin9(P1), .pin10(_7401_6_pin10), .pin11(SEL_RP), .pin12(P0),
    .pin13(_7401_6_pin13), .pin14(1'b1));
  _74175 _74175_1 (
    ._1Q(P0), ._1D(BUS0), ._2Q(P1), ._2D(BUS1), ._3Q(P2), ._3D(BUS2), ._4Q(P3), ._4D(BUS3), .VCC(1'b1),
    .GND(1'b0), .CLK(BUS__gt_P), .nCLR(nRESET));  // open: n1Q, n2Q, n3Q, n4Q
  _7401 _7401_9 (
    .pin1(nBUS3), .pin2(in_7), .pin3(in_3), .pin4(nBUS2), .pin5(in_7), .pin6(in_4), .pin7(1'b0), .pin8(in_7),
    .pin9(in_5), .pin10(nBUS1), .pin11(in_7), .pin12(in_6), .pin13(nBUS0), .pin14(1'b1));
  _74540 _74540_1 (
    .pin1(1'b0), .pin2(nT0), .pin3(nT1), .pin4(nT2), .pin5(nT3), .pin6(nT4), .pin7(nT5), .pin8(nT6),
    .pin9(nT7), .pin10(1'b0), .pin11(T7), .pin12(T6), .pin13(T5), .pin14(T4), .pin15(T3), .pin16(T2),
    .pin17(T1), .pin18(T0), .pin19(1'b0), .pin20(1'b1));
  _7401 _7401_10 (
    .pin1(pullup_19_out), .pin2(SEL_RN), .pin3(N3), .pin4(pullup_20_out), .pin5(SEL_RN), .pin6(N2),
    .pin7(1'b0), .pin8(SEL_RN), .pin9(N1), .pin10(_7401_6_pin10), .pin11(SEL_RN), .pin12(N0),
    .pin13(_7401_6_pin13), .pin14(1'b1));
  _74175 _74175_2 (
    ._1Q(N0), ._1D(BUS0), ._2Q(N1), ._2D(BUS1), ._3Q(N2), ._3D(BUS2), ._4Q(N3), ._4D(BUS3), .VCC(1'b1),
    .GND(1'b0), .CLK(nBUS__gt_N), .nCLR(nRESET));  // open: n1Q, n2Q, n3Q, n4Q
  _74540 _74540_2 (
    .pin1(1'b0), .pin2(pullup_19_out), .pin3(pullup_20_out), .pin4(_7401_6_pin10), .pin5(_7401_6_pin13),
    .pin6(nN_6_E), .pin7(nN_2_A), .pin8(nN_1_9), .pin9(N3), .pin10(1'b0), .pin11(nNBIT3), .pin12(N_1_9),
    .pin13(N_2_A), .pin14(N_6_E), .pin15(RA0), .pin16(RA1), .pin17(RA2), .pin18(RA3), .pin19(1'b0),
    .pin20(1'b1));
  nand nand_19 (INH_N, nI4, nI8, nI9);
  _74138 _74138_2 (
    .pin1(N0), .pin2(N1), .pin3(N2), .pin4(INH_N), .pin5(1'b0), .pin6(1'b1), .pin7(nN_7_F), .pin8(1'b0),
    .pin9(nN_6_E), .pin10(Cn), .pin11(nN_4_C), .pin12(nN_3_B), .pin13(nN_2_A), .pin14(nN_1_9),
    .pin15(nN_0_8), .pin16(1'b1));
  not not_23 (NBIT3, nNBIT3);
  not not_24 (not_24_out, DE_REG);
  not not_25 (not_25_out, INT_REG);
  nand nand_20 (nand_20_out, N_6_E, IF);
  _7401 _7401_11 (
    .pin1(nBUS7), .pin2(D__gt_BUS), .pin3(D_Bit_7), .pin4(nBUS6), .pin5(D__gt_BUS), .pin6(D_Bit_6),
    .pin7(1'b0), .pin8(D__gt_BUS), .pin9(D_Bit_5), .pin10(nBUS5), .pin11(D__gt_BUS), .pin12(D_Bit_4),
    .pin13(nBUS4), .pin14(1'b1));
  nand nand_21 (nand_21_out, S2, in_19);
  nand nand_22 (nand_22_out, I0, not_24_out, not_25_out);
  nand nand_23 (nand_23_out, not_24_out, INT_REG, S1);
  nand nand_24 (nand_24_out, S1, DE_REG);
  _7495 _7495_1 (
    .Q0(D_Bit_7), .P0(F7), .S(nand_20_out), .DS(1'b0), .nCP1(D_CLOCK), .nCP2(D_CLOCK), .Q1(D_Bit_6), .P1(F6),
    .Q2(D_Bit_5), .P2(F5), .Q3(D_Bit_4), .P3(F4), .VCC(1'b1), .GND(1'b0));
  nand nand_25 (nand_25_out, nand_21_out, nS0, nand_22_out, nand_23_out);
  nand nand_26 (nand_26_out, nand_23_out, nand_24_out);
  nor nor_18 (nor_18_out, D_Bit_0, D_Bit_1);
  nor nor_19 (nor_19_out, D_Bit_2, D_Bit_3);
  nor nor_20 (nor_20_out, D_Bit_4, D_Bit_5);
  nor nor_21 (nor_21_out, D_Bit_6, D_Bit_7);
  _74181 _74181_1 (
    .pin1(D_Bit_4), .pin2(BUS4), .pin3(AS3), .pin4(AS2), .pin5(AS1), .pin6(AS0), .pin7(_74181_1_pin7),
    .pin8(M), .pin9(F4), .pin10(F5), .pin11(F6), .pin12(1'b0));  // open: pin13, pin14, pin15, pin16, pin17, pin18, pin19, pin20, pin21, pin22, pin23, pin24
  _74181 _74181_2 (
    .pin1(D_Bit_0), .pin2(BUS0), .pin3(S3), .pin4(S2), .pin5(S1), .pin6(S0), .pin7(Cn), .pin8(M), .pin9(F0),
    .pin10(F1), .pin11(F2), .pin12(1'b0));  // open: pin13, pin14, pin15, pin16, pin17, pin18, pin19, pin20, pin21, pin22, pin23, pin24
  _7401 _7401_12 (
    .pin1(nBUS3), .pin2(D__gt_BUS), .pin3(D_Bit_3), .pin4(nBUS2), .pin5(D__gt_BUS), .pin6(D_Bit_2),
    .pin7(1'b0), .pin8(D__gt_BUS), .pin9(D_Bit_1), .pin10(nBUS1), .pin11(D__gt_BUS), .pin12(D_Bit_0),
    .pin13(nBUS0), .pin14(1'b1));
  nand nand_27 (nD_eq_0, nor_18_out, nor_19_out, nor_20_out, nor_21_out);
  _7474 _7474_1 (
    .pin1(nRESET), .pin2(nand_26_out), .pin3(_7474_1_pin3), .pin4(1'b1), .pin5(_7474_1_pin5),
    .pin6(_7474_1_pin6), .pin7(1'b0), .pin8(_7474_1_pin8), .pin9(_7474_1_pin9), .pin10(nRESET),
    .pin11(_7474_1_pin3), .pin12(nand_25_out), .pin13(1'b1), .pin14(1'b1));
  nand nand_28 (nS3, _7474_1_pin9, _7474_1_pin5);
  not not_26 (S3, nS3);
  _7495 _7495_2 (
    .Q0(D_Bit_3), .P0(F3), .S(nand_20_out), .DS(D_Bit_4), .nCP1(D_CLOCK), .nCP2(D_CLOCK), .Q1(D_Bit_2),
    .P1(F2), .Q2(D_Bit_1), .P2(F1), .Q3(D_Bit_0), .P3(F0), .VCC(1'b1), .GND(1'b0));
  nand nand_29 (nS2, _7474_1_pin8, _7474_1_pin5);
  not not_27 (S2, nS2);
  nand nand_30 (nS1, _7474_1_pin9, _7474_1_pin6);
  not not_28 (S1, nS1);
  nand nand_31 (nS0, _7474_1_pin8, _7474_1_pin6);
  nand nand_32 (S0, in_20, nS0);
  nand nand_33 (_7474_1_pin3, T7, in_17);
  nand nand_34 (nand_34_out, _7474_1_pin3, in_20);
  nand nand_35 (nBUS__gt_N, nand_34_out, S0);
  _74175 _74175_3 (
    ._1Q(OP0), ._1D(BUS4), ._2Q(OP1), ._2D(BUS5), ._3Q(OP2), ._3D(BUS6), ._4Q(OP3), ._4D(BUS7), .VCC(1'b1),
    .GND(1'b0), .CLK(nBUS__gt_N), .nCLR(nRESET));  // open: n1Q, n2Q, n3Q, n4Q
  nand nand_36 (nand_36_out, Cn, nN_4_C);
  nand nand_37 (nCn_plus_8, Cn_plus_8, Cn_plus_8);
  nand nand_38 (nand_38_out, N_6_E, D_Bit_0);
  nand nand_39 (nand_39_out, T5, IF);
  nand nand_40 (M, nN_3_B, nN_2_A, nN_1_9);
  nand nand_41 (AS3, nN_4_C, nN_2_A, nN_1_9);
  nand nand_42 (AS2, Cn, nN_3_B, nN_1_9);
  nand nand_43 (AS1, Cn, nN_3_B, nN_2_A, nN_1_9);
  nand nand_44 (AS0, nN_4_C, nN_2_A);
  nand nand_45 (nand_45_out, nand_36_out, Cn_plus_8);
  _74138 _74138_3 (
    .pin1(OP0), .pin2(OP1), .pin3(OP2), .pin4(OP3), .pin5(nS1), .pin6(1'b1), .pin7(nI7), .pin8(1'b0),
    .pin9(nI6), .pin10(nI5), .pin11(nI4), .pin12(nI3), .pin13(nI2), .pin14(nI1), .pin15(nI0), .pin16(1'b1));
  _74138 _74138_4 (
    .pin1(OP0), .pin2(OP1), .pin3(OP2), .pin4(nS1), .pin5(1'b0), .pin6(OP3), .pin7(nIF), .pin8(1'b0),
    .pin9(nIE), .pin10(nID), .pin11(nIC), .pin12(nIB), .pin13(nIA), .pin14(nI9), .pin15(nI8), .pin16(1'b1));
  nand nand_46 (nand_46_out, nand_45_out, nand_38_out);
  PullUp pullup_23 (.out(nBUS7));
  PullUp pullup_24 (.out(nBUS6));
  PullUp pullup_25 (.out(nBUS5));
  PullUp pullup_26 (.out(nBUS4));
  PullUp pullup_27 (.out(pullup_27_out));
  _7474 _7474_2 (
    .pin1(pullup_27_out), .pin2(nand_46_out), .pin3(nand_39_out), .pin4(pullup_27_out), .pin5(DF),
    .pin7(1'b0), .pin10(1'b0), .pin11(1'b0), .pin12(1'b0), .pin13(1'b0), .pin14(1'b1));  // open: pin6, pin8, pin9
  PullUp pullup_28 (.out(nBUS3));
  PullUp pullup_29 (.out(nBUS2));
  _74540 _74540_3 (
    .pin1(in_25), .pin2(nBUS7), .pin3(nBUS6), .pin4(nBUS5), .pin5(nBUS4), .pin6(nBUS3), .pin7(nBUS2),
    .pin8(nBUS1), .pin9(nBUS0), .pin10(1'b0), .pin11(BUS0), .pin12(BUS1), .pin13(BUS2), .pin14(BUS3),
    .pin15(BUS4), .pin16(BUS5), .pin17(BUS6), .pin18(BUS7), .pin19(in_25), .pin20(1'b1));
  PullUp pullup_30 (.out(nBUS1));
  PullUp pullup_31 (.out(nBUS0));
  _74540 _74540_4 (
    .pin1(1'b0), .pin2(nI0), .pin3(nI2), .pin4(nI4), .pin5(nI6), .pin6(nI7), .pin7(nI8), .pin8(nI9),
    .pin9(nIF), .pin10(1'b0), .pin11(IF), .pin12(I9), .pin13(I8), .pin14(I7), .pin15(I6), .pin16(I4),
    .pin17(I2), .pin18(I0), .pin19(1'b0), .pin20(1'b1));
  nand nand_47 (nand_47_out, nIA, nIB, nIC);
  not not_29 (nIABC, nand_47_out);
  nand nand_48 (nI6_NBIT3, I6, NBIT3);
  nand nand_49 (T__gt_BUS, nRESTORE, nRESTORE);
  nand nand_50 (N__gt_BUS, nID, nIE);
  nand nand_51 (D__gt_BUS, nI5, nIABC);
  nand nand_52 (A1__gt_BUS, nI9, nI9);
  nand nand_53 (A0__gt_BUS, nIB, nIB);
  nand nand_54 (INH_N_DECODE, nI9, nIB, nI4);
  nand nand_55 (nand_55_out, I7, NBIT3);
  nand nand_56 (nand_56_out, nT5, nand_57_out);
  nand nand_57 (nand_57_out, nand_56_out, nT7);
  nand nand_58 (BUS__gt_R, nIABC, nMANUAL, nI3_COND_eq_1);
  nand nand_59 (nand_59_out, nI3, nI4);
  nand nand_60 (SEL_RP, nI3, nS0);
  nand nand_61 (SEL_RX, nI6, nI7, nIF);
  nand nand_62 (nand_62_out, nT4, nand_63_out);
  nand nand_63 (nand_63_out, nand_62_out, nT6);
  nand nand_64 (nRESTORE, I7, NBIT3);
  nand nand_65 (nand_65_out, NBIT3, nI6);
  nand nand_66 (nPX__gt_T, T4, S3);
  nand nand_67 (M__gt_BUS, nI3I4RESTORE, nI0, nIF, nS0, nDEOUT, nI6_NBIT3);
  not not_30 (not_30_out, INH_N_DECODE);
  and and_9 (and_9_out, nS3, nand_55_out);
  nand nand_68 (nand_68_out, nand_56_out, I3_COND_eq_1);
  nor nor_22 (SEL_RN, SEL_RP, S2, SEL_RX);
  not not_31 (PX__gt_T, nPX__gt_T);
  nand nand_69 (nand_69_out, not_30_out, nIF);
  nor nor_23 (nI3I4RESTORE, T4, nand_59_out);
  nand nand_70 (nand_70_out, nRESTORE, nand_65_out, nI5, nDEIN);
  nand nand_71 (nand_71_out, nID, and_9_out);
  nand nand_72 (nand_72_out, and_9_out, nIE);
  and and_10 (D_CLOCK, nand_69_out, T6);
  nand nand_73 (INH_R10, nand_68_out, nIA, in_24, nIC);
  nand nand_74 (INH_R01, nIC, nIB, in_23);
  nand nand_75 (INH_R00, in_23, nIB);
  nand nand_76 (nand_76_out, nand_62_out, nand_70_out);
  nand nand_77 (nand_77_out, T7, nand_71_out);
  and and_11 (BUS__gt_X, nand_72_out, T7);
  nand nand_78 (nand_78_out, nI6_NBIT3, nI1, S1, nI3I4RESTORE);
  and and_12 (nWE, in_21, nand_76_out);
  nand nand_79 (BUS__gt_P, in_18, nand_77_out);
  nor nor_24 (nor_24_out, I2, nand_78_out, BUS__gt_R);
  nand nand_80 (nand_80_out, BUS__gt_R, T3);
  nand nand_81 (nC_plus_1, nI3_COND_eq_1, T3, nand_78_out);
  nand nand_82 (nC_1, T3, I2);
  not not_32 (not_32_out, nor_24_out);
  nand nand_83 (nand_83_out, T6, not_32_out);
  nand nand_84 (nand_84_out, in_16, nRESET, nand_83_out);
  nand nand_85 (RES_C, nRESET, nand_80_out);
  nand nand_86 (nRWR, nS3, nand_84_out);

  // Other names for the same wires on the sheet: EF1 = in_13; EF2 = in_12; EF3 = in_11; EF4 = in_10;
  //   INH_R11 = INH_R10; LOAD = in_19; MANUAL = in_22; NBIT0 = N0; NBIT1 = N1; NBIT2 = N2; nCLR = nRESET;
  //   nCLR_PULSE = nRESET; nINREQUEST = in_8; nINTREG = in_14; nN_5_D = Cn; nOUTREQUEST = in_9; nRESUME = in_15;
  //   nSAVE = nRESTORE; nTP0 = nT0; nTP1 = nT1; nTP2 = nT2; nTP3 = nT3; nTP4 = nT4; nTP5 = nT5; nTP6 = nT6;
  //   nTP7 = nT7; R0E = in_24; R1E = in_23; REPEAT = in_17; TP0 = T0; TP1 = T1; TP2 = T2; TP3 = T3; TP4 = T4;
  //   TP5 = T5; TP6 = T6; TP7 = T7; WI = in_20; WM = in_21; WP = in_18; WR = in_16

  // Notes on the sheet:
  //   clk: Hz: 8
  //   in_8: default 1
  //   in_9: default 1
  //   in_14: default 1
  //   in_15: default 1
  //   in_16: default 1
  //   in_17: default 1
  //   in_18: default 1
  //   in_19: default 1
  //   in_20: default 1
  //   in_21: default 1
  //   in_22: default 1
  //   in_23: default 1
  //   in_24: default 1
  //   in_25: default 1
  //   nRESET: default 1
  //   CURRENT ADDRESS
  //   I REG
  //   N REG
  //   X REG
  //   BUS DATA
  //   P REG
  //   PC REG
  //   COUNTER OUTPUT
  //   REG OUTPUT
  //   REG INPUTS
  //   LOGIC 7 External Interface
  //   LOGIC 3 Memory
  //   3  7400
  //   2   7475
  //   1   74151
  //   1   7402
  //   Total 7
  //   LOGIC 8 Channel Control
  //   LOGIC 4 Register Stack
  //   A->C
  //   16 x 16-BIT RAM
  //   U/D COUNTER
  //   1  7400
  //   4   7401
  //   4  7402
  //   2  7408
  //   4  7475
  //   4  7489
  //   4  74193
  //   Total  23
  //   LOGIC 9 Timing Generator
  //   LOGIC 5 P-X-N-T
  //   REG TH
  //   REG TL
  //   REG X
  //   REG P
  //   REG N
  //   6  7401
  //   1  74138
  //   5  74173
  //   1  74540
  //   Total 13
  //   1  7400
  //   1  74138
  //   1  74163
  //   1  74540
  //   Total 4
  //   LOGIC 10 I, S Decode
  //   LOGIC 6 D Register, ALU
  //   AND
  //   OR
  //   XOR
  //   ADD
  //   SUB
  //   3  7400
  //   1  7404
  //   1  7410
  //   1  7420
  //   1  7474
  //   1  74175
  //   2  74138
  //   1  74540
  //   Total 11
  //   2  7400
  //   2  7401
  //   1  7402
  //   1  7410
  //   1  7420
  //   1  7474
  //   2   7495
  //   2   74181
  //   1  74540
  //   Total 8
  //   LOGIC 11 Bus Select
  //   LOGIC 12 R-C Control
  //   LOGIC 13 M-D-MSC Control
  //   Memory Write
  //   1  7408
  //   1  7430
  //   3  7400
  //   Total 5
  //   3  7400
  //   2   7410
  //   1  7420
  //   1  7427
  //   Total 7
  //   2  7400
  //   1  7420
  //   1  7408
  //   Total 4
endmodule
